// Logisim project circuits.circ as structural Verilog
module Q1_a (
  input  A,
  input  B,
  input  C,
  input  D,
  output out_5
);

  wire and_1_out, not_1_out, not_2_out, not_3_out;

  not not_1 (not_1_out, B);
  not not_2 (not_2_out, C);
  not not_3 (not_3_out, D);
  and and_1 (and_1_out, not_1_out, not_1_out, A, not_3_out);
  or or_1 (out_5, not_2_out, and_1_out);
endmodule

module Q1_b (
  input  A,
  input  B,
  input  C,
  input  D,
  output out_5
);

  wire and_1_out, and_2_out, and_3_out, not_1_out;

  and and_1 (and_1_out, A, not_1_out);
  not not_1 (not_1_out, B);
  and and_2 (and_2_out, B, D);
  and and_3 (and_3_out, C, D);
  or or_1 (out_5, and_1_out, and_2_out, and_3_out);
endmodule

module Q1_3_1 (
  input  B,
  input  A,
  input  D,
  input  C,
  output out_5
);

  wire nand_1_out, nand_2_out, nand_3_out;

  nand nand_1 (nand_1_out, B, B);
  nand nand_2 (nand_2_out, D, D);
  nand nand_3 (nand_3_out, nand_1_out, A, nand_2_out);
  nand nand_4 (out_5, nand_3_out, C);
endmodule

module Q1_3_2 (
  input  A,
  input  B,
  input  C,
  input  D,
  output out_5
);

  wire nand_1_out, nand_2_out, nand_3_out, nand_4_out;

  nand nand_1 (nand_1_out, B, B);
  nand nand_2 (nand_2_out, A, nand_1_out);
  nand nand_3 (nand_3_out, B, D);
  nand nand_4 (nand_4_out, C, D);
  nand nand_5 (out_5, nand_2_out, nand_3_out, nand_4_out);
endmodule

module Q2_5_1 (
  input  A,
  input  B,
  input  C,
  input  D,
  output out_5
);

  wire nand_1_out, nand_2_out, nand_3_out, not_1_out, not_2_out;

  not not_1 (not_1_out, B);
  not not_2 (not_2_out, D);
  nand nand_1 (nand_1_out, A, D);
  nand nand_2 (nand_2_out, B, C);
  nand nand_3 (nand_3_out, not_1_out, not_2_out);
  nand nand_4 (out_5, nand_1_out, nand_2_out, nand_3_out);
endmodule

module Q2_5_2 (
  input  A,
  input  B,
  input  C,
  input  D,
  output out_5
);

  wire nand_1_out, nand_2_out, nand_3_out, nand_4_out, nand_5_out, nand_6_out, nand_7_out;

  nand nand_1 (nand_1_out, A, A);
  nand nand_2 (nand_2_out, C, C);
  nand nand_3 (nand_3_out, B, B);
  nand nand_4 (nand_4_out, D, D);
  nand nand_5 (nand_5_out, nand_3_out, nand_1_out, D);
  nand nand_6 (nand_6_out, nand_1_out, nand_2_out, D);
  nand nand_7 (nand_7_out, B, nand_2_out, nand_4_out);
  nand nand_8 (out_5, nand_5_out, nand_6_out, nand_7_out);
endmodule
