// Logisim project hw3.circ as structural Verilog: 1 circuit, main circuit main
module main (
  input  a,
  output X,
  output Y,
  output Z,
  output n2,
  output n1,
  output n0
);

  wire and_1_out, and_2_out, and_4_out, and_5_out, and_6_out, and_7_out, and_8_out, and_9_out, and_10_out,
       and_11_out, and_12_out, and_13_out, clock_1_out, not_1_out, not_2_out, not_3_out, not_4_out, or_3_out,
       or_4_out, or_5_out, S0_q, S1_q, S2_q, xor_1_out, xor_2_out, xor_3_out;

  or or_1 (n2, and_1_out, and_2_out);
  and and_1 (and_1_out, or_3_out, S1_q);
  and and_2 (and_2_out, S2_q, not_3_out);
  or or_2 (n1, and_6_out, and_7_out, and_8_out);
  and and_3 (n0, xor_2_out, or_4_out);
  or or_3 (or_3_out, and_4_out, and_5_out);
  and and_4 (and_4_out, a, not_2_out, S0_q);
  and and_5 (and_5_out, not_1_out, S2_q, not_4_out);
  xor xor_1 (xor_1_out, S0_q, S2_q);
  and and_6 (and_6_out, xor_1_out, not_1_out, S1_q);
  and and_7 (and_7_out, not_3_out, S0_q, not_2_out, a);
  and and_8 (and_8_out, not_2_out, S1_q, not_4_out);
  xor xor_2 (xor_2_out, a, S0_q);
  or or_4 (or_4_out, not_2_out, not_3_out);
  Clock clock_1 (.out(clock_1_out));
  not not_1 (not_1_out, a);
  not not_2 (not_2_out, S2_q);
  D_Flip_Flop S2 (.clk(clock_1_out), .D(n2), .Q(S2_q));  // open: Qn, preset, en, reset
  D_Flip_Flop S1 (.clk(clock_1_out), .D(n1), .Q(S1_q));  // open: Qn, preset, en, reset
  D_Flip_Flop S0 (.clk(clock_1_out), .D(n0), .Q(S0_q));  // open: Qn, preset, en, reset
  not not_3 (not_3_out, S1_q);
  not not_4 (not_4_out, S0_q);
  and and_9 (and_9_out, not_4_out, S1_q);
  and and_10 (and_10_out, S0_q, not_3_out, S2_q);
  and and_11 (and_11_out, not_3_out, S0_q);
  and and_12 (and_12_out, not_3_out, S0_q);
  xor xor_3 (xor_3_out, S1_q, S2_q);
  or or_5 (or_5_out, S1_q, and_11_out);
  or or_6 (Z, and_12_out, and_13_out);
  and and_13 (and_13_out, xor_3_out, not_4_out);
  or or_7 (X, and_9_out, and_10_out);
  and and_14 (Y, not_2_out, or_5_out);
endmodule
