// Logisim project circuit.circ as structural Verilog: 1 circuit, main circuit main
// 4
module main (
  input  cl,
  input  ld,
  input  sw,
  input  L0,
  input  L1,
  input  L2,
  input  L3,
  input  L4,
  input  L5,
  input  _0_pin
);

  wire and_1_out, and_2_out, clock_out, d_ff_1_q, d_ff_2_q, d_ff_3_q, d_ff_4_q, d_ff_5_q, d_ff_6_q,
       multiplexer_1_out, multiplexer_2_out, multiplexer_3_out, multiplexer_4_out, multiplexer_5_out,
       multiplexer_6_out, not_1_out, not_2_out;
  wire [1:0] or_1_out;

  not not_1 (not_1_out, cl);
  not not_2 (not_2_out, ld);
  and and_1 (and_1_out, ld, not_1_out);
  or or_1 (or_1_out[0], and_1_out, and_2_out);
  and and_2 (and_2_out, not_1_out, not_2_out, sw);
  or or_2 (or_1_out[1], and_2_out, cl);
  Clock clock (.out(clock_out));
  Multiplexer #(.select(2), .enable("false")) multiplexer_1 (
    .in0(d_ff_1_q), .in1(L0), .in2(_0_pin), .in3(d_ff_2_q), .out(multiplexer_1_out), .sel(or_1_out));
  D_Flip_Flop d_ff_1 (.clk(clock_out), .D(multiplexer_1_out), .Q(d_ff_1_q));  // open: Qn, preset, en, reset
  Multiplexer #(.select(2), .enable("false")) multiplexer_2 (
    .in0(d_ff_2_q), .in1(L1), .in2(_0_pin), .in3(d_ff_1_q), .out(multiplexer_2_out), .sel(or_1_out));
  D_Flip_Flop d_ff_2 (.clk(clock_out), .D(multiplexer_2_out), .Q(d_ff_2_q));  // open: Qn, preset, en, reset
  Multiplexer #(.select(2), .enable("false")) multiplexer_3 (
    .in0(d_ff_3_q), .in1(L2), .in2(_0_pin), .in3(d_ff_4_q), .out(multiplexer_3_out), .sel(or_1_out));
  D_Flip_Flop d_ff_3 (.clk(clock_out), .D(multiplexer_3_out), .Q(d_ff_3_q));  // open: Qn, preset, en, reset
  Multiplexer #(.select(2), .enable("false")) multiplexer_4 (
    .in0(d_ff_4_q), .in1(L3), .in2(_0_pin), .in3(d_ff_3_q), .out(multiplexer_4_out), .sel(or_1_out));
  D_Flip_Flop d_ff_4 (.clk(clock_out), .D(multiplexer_4_out), .Q(d_ff_4_q));  // open: Qn, preset, en, reset
  Multiplexer #(.select(2), .enable("false")) multiplexer_5 (
    .in0(d_ff_5_q), .in1(L4), .in2(_0_pin), .in3(d_ff_6_q), .out(multiplexer_5_out), .sel(or_1_out));
  D_Flip_Flop d_ff_5 (.clk(clock_out), .D(multiplexer_5_out), .Q(d_ff_5_q));  // open: Qn, preset, en, reset
  Multiplexer #(.select(2), .enable("false")) multiplexer_6 (
    .in0(d_ff_6_q), .in1(L5), .in2(_0_pin), .in3(d_ff_5_q), .out(multiplexer_6_out), .sel(or_1_out));
  D_Flip_Flop d_ff_6 (.clk(clock_out), .D(multiplexer_6_out), .Q(d_ff_6_q));  // open: Qn, preset, en, reset
endmodule
