// Logisim project lab1.circ as structural Verilog
module main (
  input  a,
  input  b,
  input  c,
  input  d,
  output out_5
);

  xor odd_parity_1 (out_5, a, b, c, d);
endmodule
