// Logisim project lab2.circ as structural Verilog: 1 circuit, main circuit main
module main (
  input  w,
  input  x,
  input  y,
  input  z,
  output P,
  output T
);

  wire not_1_out, not_2_out, not_3_out;

  not not_1 (not_1_out, x);
  not not_2 (not_2_out, y);
  not not_3 (not_3_out, z);
  and and_1 (P, not_3_out, not_1_out);
  and and_2 (T, not_1_out, not_2_out);
endmodule
