// Logisim project lab3.circ as structural Verilog: 1 circuit, main circuit main
module main (
  input  w,
  input  x,
  input  y,
  input  z,
  input  t
);

  wire and_1_out, and_2_out, and_3_out, and_4_out, and_5_out, and_6_out, and_7_out, and_8_out, not_1_out,
       not_2_out, not_3_out, not_5_out, or_1_out, or_2_out;

  not not_1 (not_1_out, x);
  not not_2 (not_2_out, y);
  not not_3 (not_3_out, z);
  not not_4 (not_1_out, t);
  and and_1 (and_1_out, z, not_1_out, not_1_out, not_2_out);
  and and_2 (and_2_out, not_1_out, not_2_out, z, not_1_out);
  and and_3 (and_3_out, not_2_out, t, not_3_out, not_1_out);
  and and_4 (and_4_out, not_1_out, not_3_out, y, z, t);
  and and_5 (and_5_out, not_1_out, y, t, z);
  and and_6 (and_6_out, not_1_out, not_1_out, not_2_out, x, not_3_out);
  or or_1 (or_1_out, and_1_out, and_2_out, and_3_out, and_4_out);
  not not_5 (not_5_out, w);
  or or_2 (or_2_out, and_5_out, and_6_out);
  and and_7 (and_7_out, or_1_out, w);
  and and_8 (and_8_out, not_5_out, or_2_out, or_2_out);
  // OR_Gate or_3 has open pins: in1=and_7_out, in3=and_8_out, out=open
endmodule
