// Logisim project lab4.circ as structural Verilog: 1 circuit, main circuit main
module main (
  input  a,
  input  b
);

  wire and_1_out, and_2_out, and_3_out, and_4_out, and_5_out, and_6_out, not_1_out, not_2_out, not_3_out,
       not_4_out, not_5_out, or_1_out, or_2_out, S0_q, S1_q, undriven;

  not not_1 (not_1_out, a);
  and and_1 (and_1_out, a, not_3_out, S0_q);
  and and_2 (and_2_out, b, S1_q);
  and and_3 (and_3_out, not_1_out, S1_q, not_2_out);
  not not_2 (not_2_out, S0_q);
  not not_3 (not_3_out, S1_q);
  or or_1 (or_1_out, and_1_out, and_2_out, and_3_out);
  D_Flip_Flop S1 (.clk(undriven), .D(or_1_out), .Q(S1_q));  // open: Qn, preset, en, reset
  not not_4 (not_4_out, b);
  not not_5 (not_5_out, S1_q);
  and and_4 (and_4_out, a, not_4_out, not_5_out);
  and and_5 (and_5_out, S1_q, b, S0_q);
  and and_6 (and_6_out, S1_q, not_1_out, b);
  D_Flip_Flop S0 (.clk(undriven), .D(or_2_out), .Q(S0_q));  // open: Qn, preset, en, reset
  or or_2 (or_2_out, and_4_out, and_5_out, and_6_out);
  LED led_1 (.in(S1_q));
endmodule
