// Logisim project lab_circ.circ as structural Verilog: 1 circuit, main circuit main
module main (
  input  goi,
  input  [7:0] Xi,
  input  [7:0] yi,
  input  [7:0] in_4,
  input  [7:0] in_5,
  input  [7:0] in_6,
  input  [7:0] in_7,
  output [7:0] z,
  output [2:0] z_2
);

  wire and_1_out, and_2_out, and_3_out, and_4_out, and_5_out, and_6_out, and_7_out, and_8_out, and_9_out,
       clock_1_out, comparator_1_gt, comparator_2_gt, not_1_out, not_2_out, not_3_out, or_4_out, or_5_out;
  wire [2:0] or_1_out;
  wire [7:0] adder_1_out, adder_2_out, diff2_reg_q, diff_ref_q, multiplexer_1_out, multiplexer_2_out,
       subtractor_1_out, subtractor_2_out, x_reg_q, y_reg_q;

  or or_1 (or_1_out[0], and_1_out, and_2_out);
  and and_1 (and_1_out, not_3_out, z_2[1], or_4_out);
  or or_2 (or_1_out[1], and_3_out, z_2[1], and_4_out);
  or or_3 (or_1_out[2], and_5_out, and_6_out);
  Clock clock_1 (.out(clock_1_out));
  or or_4 (or_4_out, comparator_2_gt, comparator_1_gt);
  and and_2 (and_2_out, goi, z_2[2], z_2[1], z_2[0]);
  and and_3 (and_3_out, comparator_1_gt, z_2[0], z_2[1], z_2[2]);
  and and_4 (and_4_out, z_2[0], not_2_out, not_3_out);
  and and_5 (and_5_out, z_2[0], z_2[1], not_3_out);
  and and_6 (and_6_out, not_2_out, z_2[2]);
  Register #(.width(3)) register_1 (.D(or_1_out), .Q(z_2), .clk(clock_1_out));  // open: en, clr
  not not_1 (not_1_out, z_2[0]);
  not not_2 (not_2_out, z_2[1]);
  and and_7 (and_7_out, not_3_out, z_2[0], not_2_out);
  not not_3 (not_3_out, z_2[2]);
  and and_8 (and_8_out, not_1_out, z_2[1], z_2[2]);
  or or_5 (or_5_out, and_7_out, and_8_out);
  Register x_reg (.D(Xi), .en(and_7_out), .Q(x_reg_q), .clk(clock_1_out));  // open: clr
  Subtractor subtractor_1 (.a(x_reg_q), .b(y_reg_q), .out(subtractor_1_out));  // open: bin, bout
  Register y_reg (.D(yi), .en(and_7_out), .Q(y_reg_q), .clk(clock_1_out));  // open: clr
  and and_9 (and_9_out, z_2[2], not_2_out);
  Register diff2_reg (.D(diff_ref_q), .en(and_7_out), .Q(diff2_reg_q), .clk(clock_1_out));  // open: clr
  Multiplexer #(.width(8), .enable("false")) multiplexer_1 (
    .in0(adder_2_out), .in1(adder_1_out), .out(multiplexer_1_out), .sel(z_2[0]));
  Register z_reg (.D(multiplexer_1_out), .en(and_9_out), .Q(z), .clk(clock_1_out), .clr(and_7_out));
  Adder adder_1 (.a(z), .b(in_5), .out(adder_1_out));  // open: cin, cout
  Adder adder_2 (.a(z), .b(diff2_reg_q), .out(adder_2_out));  // open: cin, cout
  Multiplexer #(.width(8), .enable("false")) multiplexer_2 (
    .in0(subtractor_1_out), .in1(subtractor_2_out), .out(multiplexer_2_out), .sel(z_2[2]));
  Register diff_ref (.D(multiplexer_2_out), .en(or_5_out), .Q(diff_ref_q), .clk(clock_1_out));  // open: clr
  Subtractor subtractor_2 (.a(diff_ref_q), .b(in_4), .out(subtractor_2_out));  // open: bin, bout
  Comparator comparator_1 (.a(diff_ref_q), .b(in_6), .gt(comparator_1_gt));  // open: eq, lt
  Comparator comparator_2 (.a(diff_ref_q), .b(in_7), .gt(comparator_2_gt));  // open: eq, lt
endmodule
